// Logisim project alu.circ as structural Verilog: 1 circuit, main circuit alu
module alu (
  input  [31:0] A,
  input  [31:0] B,
  input  [3:0] ALUSel,
  output [31:0] ALUResult
);

  wire comparator_1_lt;
  wire [31:0] add0, and0, mul0, mulh0, mulhu0, or0, sll0, slt0, sra0, srl0, sub0, Unused, xor0;
  wire [63:0] bit_extender_1_out, bit_extender_2_out, bit_extender_3_out, bit_extender_4_out,
       multiplier_1_cout, multiplier_2_cout;

  Adder #(.width(32)) adder_1 (.a(A), .b(B), .out(add0));  // open: cin, cout
  Comparator #(.width(32)) comparator_1 (.a(A), .b(B), .lt(comparator_1_lt));  // open: gt, eq
  assign xor0 = A ^ B;  // XOR_Gate xor_1, 32 bits wide
  assign or0 = A | B;  // OR_Gate or_1, 32 bits wide
  assign and0 = A & B;  // AND_Gate and_1, 32 bits wide
  assign bit_extender_1_out = {{32{A[31]}}, A};  // Bit_Extender bit_extender_1
  assign bit_extender_2_out = {{32{B[31]}}, B};  // Bit_Extender bit_extender_2
  assign bit_extender_3_out = {{32{1'b0}}, A};  // Bit_Extender bit_extender_3
  assign bit_extender_4_out = {{32{1'b0}}, B};  // Bit_Extender bit_extender_4
  Subtractor #(.width(32)) subtractor_1 (.a(A), .b(B), .out(sub0));  // open: bin, bout
  Shifter #(.width(32)) shifter_1 (.in(A), .\dist (B[4:0]), .out(sll0));
  assign slt0 = {{31{1'b0}}, comparator_1_lt};  // Bit_Extender bit_extender_5
  Shifter #(.shift("lr"), .width(32)) shifter_2 (.in(A), .\dist (B[4:0]), .out(srl0));
  Multiplier #(.mode("twosComplement"), .width(64)) multiplier_1 (
    .a(bit_extender_1_out), .b(bit_extender_2_out), .out({mulh0, mul0}), .cin({64{1'b0}}),
    .cout(multiplier_1_cout));
  Multiplier #(.width(64)) multiplier_2 (
    .a(bit_extender_3_out), .b(bit_extender_4_out), .out({mulhu0, mul0}), .cin({64{1'b0}}),
    .cout(multiplier_2_cout));
  Shifter #(.shift("ar"), .width(32)) shifter_3 (.in(A), .\dist (B[4:0]), .out(sra0));
  Multiplexer #(.select(4), .width(32)) multiplexer_1 (
    .in0(add0), .in1(sll0), .in2(slt0), .in3(Unused), .in4(xor0), .in5(srl0), .in6(or0), .in7(and0),
    .in8(mul0), .in9(mulh0), .in10(Unused), .in11(mulhu0), .in12(sub0), .in13(sra0), .in14(Unused), .in15(B),
    .out(ALUResult), .sel(ALUSel));

  // Other names for the same wires on the sheet: bsel0[31:0] = B

  // Notes on the sheet:
  //   INPUTS to your circuit
  //   DON'T CHANGE THE LOCATIONS OF THE INPUTS AND OUTPUTS!
  //   OUTPUT from your circuit
endmodule
