// Logisim project branch-comp.circ as structural Verilog: 1 circuit, main circuit branch_comp
module branch_comp (
  input  [31:0] BrData1,
  input  [31:0] BrData2,
  input  BrUn,
  output BrEq,
  output BrLt
);

  wire SignBrEq, SignBrLt, UnSignBrEq, UnSignBrLt;

  Comparator #(.width(32)) comparator_1 (.a(BrData1), .b(BrData2), .eq(SignBrEq), .lt(SignBrLt));  // open: gt
  Comparator #(.mode("unsigned"), .width(32)) comparator_2 (
    .a(BrData1), .b(BrData2), .eq(UnSignBrEq), .lt(UnSignBrLt));  // open: gt
  Multiplexer multiplexer_1 (.in0(SignBrEq), .in1(UnSignBrEq), .out(BrEq), .sel(BrUn));
  Multiplexer multiplexer_2 (.in0(SignBrLt), .in1(UnSignBrLt), .out(BrLt), .sel(BrUn));

  // Notes on the sheet:
  //   INPUTS to your circuit
  //   DON'T CHANGE THE LOCATIONS OF THE INPUTS AND OUTPUTS!
  //   OUTPUT from your circuit
endmodule
