// Logisim project control-logic.circ as structural Verilog: 1 circuit, main circuit control_logic
module control_logic (
  input  [31:0] Instruction,
  input  BrEq,
  input  BrLt,
  output PCSel,
  output RegWEn,
  output [2:0] ImmSel,
  output BrUn,
  output ASel,
  output BSel,
  output [3:0] ALUSel,
  output MemWEn,
  output [1:0] WBSel
);

  wire and_33_out, bge_out, bgeu_out, bne_out, is_add, is_addi, is_and, is_andi, is_auipc, is_beq, is_bge,
       is_bgeu, is_blt, is_bltu, is_bne, is_jal, is_jalr, is_lb, is_lh, is_lui, is_lw, is_mul, is_mulh,
       is_mulhu, is_or, is_ori, is_sb, is_sh, is_sll, is_slli, is_slt, is_slti, is_sra, is_srai, is_srl,
       is_srli, is_sub, is_sw, is_xor, is_xori, isB_Type, isFunct3_0, isFunct3_1, isFunct3_2, isFunct3_3,
       isFunct3_4, isFunct3_5, isFunct3_6, isFunct3_7, isFunct7_0x00, isFunct7_0x01, isFunct7_0x20,
       isI_Type0, isI_Type1, isI_Type2, isR_Type, isS_Type, multiplexer_1_out;
  wire [5:0] Rom_input;
  wire [15:14] rom_1_data;

  Decoder #(.select(3)) decoder_1 (
    .out0(isFunct3_0), .out1(isFunct3_1), .out2(isFunct3_2), .out3(isFunct3_3), .out4(isFunct3_4),
    .out5(isFunct3_5), .out6(isFunct3_6), .out7(isFunct3_7), .sel(Instruction[14:12]), .en(1'b1));
  Comparator #(.mode("unsigned"), .width(7)) comparator_1 (
    .a(7'b0110011), .b(Instruction[6:0]), .eq(isR_Type));  // open: gt, lt
  Comparator #(.mode("unsigned"), .width(7)) comparator_2 (
    .a(7'b0000011), .b(Instruction[6:0]), .eq(isI_Type0));  // open: gt, lt
  Comparator #(.mode("unsigned"), .width(7)) comparator_3 (
    .a(7'b0010011), .b(Instruction[6:0]), .eq(isI_Type1));  // open: gt, lt
  Comparator #(.mode("unsigned"), .width(7)) comparator_4 (
    .a(7'b0100011), .b(Instruction[6:0]), .eq(isS_Type));  // open: gt, lt
  Comparator #(.mode("unsigned"), .width(7)) comparator_5 (
    .a(7'b1100011), .b(Instruction[6:0]), .eq(isB_Type));  // open: gt, lt
  Comparator #(.mode("unsigned"), .width(7)) comparator_6 (
    .a(7'b0010111), .b(Instruction[6:0]), .eq(is_auipc));  // open: gt, lt
  Comparator #(.mode("unsigned"), .width(7)) comparator_7 (
    .a(7'b0110111), .b(Instruction[6:0]), .eq(is_lui));  // open: gt, lt
  Comparator #(.mode("unsigned"), .width(7)) comparator_8 (
    .a(7'b1101111), .b(Instruction[6:0]), .eq(is_jal));  // open: gt, lt
  Comparator #(.mode("unsigned"), .width(7)) comparator_9 (
    .a(7'b1100111), .b(Instruction[6:0]), .eq(isI_Type2));  // open: gt, lt
  Comparator #(.mode("unsigned"), .width(7)) comparator_10 (
    .a({7{1'b0}}), .b(Instruction[31:25]), .eq(isFunct7_0x00));  // open: gt, lt
  Comparator #(.mode("unsigned"), .width(7)) comparator_11 (
    .a(7'b0000001), .b(Instruction[31:25]), .eq(isFunct7_0x01));  // open: gt, lt
  Comparator #(.mode("unsigned"), .width(7)) comparator_12 (
    .a(7'b0100000), .b(Instruction[31:25]), .eq(isFunct7_0x20));  // open: gt, lt
  ROM #(.addrWidth(6), .dataWidth(16)) rom_1 (
    .addr(Rom_input), .data({rom_1_data, WBSel, MemWEn, ALUSel, BSel, ASel, BrUn, ImmSel, RegWEn}));
  and and_1 (is_add, isR_Type, isFunct3_0, isFunct7_0x00);
  and and_2 (is_mul, isR_Type, isFunct3_0, isFunct7_0x01);
  and and_3 (is_sub, isR_Type, isFunct3_0, isFunct7_0x20);
  and and_4 (is_sll, isR_Type, isFunct3_1, isFunct7_0x00);
  and and_5 (is_mulh, isR_Type, isFunct3_1, isFunct7_0x01);
  and and_6 (is_mulhu, isR_Type, isFunct3_3, isFunct7_0x01);
  and and_7 (is_slt, isR_Type, isFunct3_2, isFunct7_0x00);
  and and_8 (is_xor, isR_Type, isFunct3_4, isFunct7_0x00);
  and and_9 (is_srl, isR_Type, isFunct3_5, isFunct7_0x00);
  and and_10 (is_sra, isR_Type, isFunct3_5, isFunct7_0x20);
  and and_11 (is_or, isR_Type, isFunct3_6, isFunct7_0x00);
  and and_12 (is_and, isR_Type, isFunct3_7, isFunct7_0x00);
  and and_13 (is_lb, isI_Type0, isFunct3_0);
  and and_14 (is_lh, isI_Type0, isFunct3_1);
  and and_15 (is_lw, isI_Type0, isFunct3_2);
  and and_16 (is_addi, isI_Type1, isFunct3_0);
  and and_17 (is_slli, isI_Type1, isFunct3_1, isFunct7_0x00);
  and and_18 (is_slti, isI_Type1, isFunct3_2);
  and and_19 (is_xori, isI_Type1, isFunct3_4);
  and and_20 (is_srli, isI_Type1, isFunct3_5, isFunct7_0x00);
  and and_21 (is_srai, isI_Type1, isFunct3_5, isFunct7_0x20);
  and and_22 (is_ori, isI_Type1, isFunct3_6);
  and and_23 (is_andi, isI_Type1, isFunct3_7);
  Multiplexer #(.select(3)) multiplexer_1 (
    .in0(BrEq), .in1(bne_out), .in2(1'b0), .in3(1'b0), .in4(BrLt), .in5(bge_out), .in6(BrLt), .in7(bgeu_out),
    .out(multiplexer_1_out), .sel(Instruction[14:12]));
  and and_24 (is_sb, isS_Type, isFunct3_0);
  and and_25 (is_sh, isS_Type, isFunct3_1);
  and and_26 (is_sw, isS_Type, isFunct3_2);
  and and_27 (is_beq, isB_Type, isFunct3_0);
  and and_28 (is_bne, isB_Type, isFunct3_1);
  and and_29 (is_blt, isB_Type, isFunct3_4);
  and and_30 (is_bge, isB_Type, isFunct3_5);
  and and_31 (is_bltu, isB_Type, isFunct3_6);
  and and_32 (is_bgeu, isB_Type, isFunct3_7);
  and and_33 (and_33_out, isB_Type, multiplexer_1_out);
  or or_1 (PCSel, is_jal, isI_Type2, and_33_out);
  and and_34 (is_jalr, isI_Type2, isFunct3_0);
  not not_1 (bne_out, BrEq);
  not not_2 (bge_out, BrLt);
  not not_3 (bgeu_out, BrLt);
  Priority_Encoder #(.select_enc(6)) priority_encoder_1 (
    .in0(is_add), .in1(is_mul), .in2(is_sub), .in3(is_sll), .in4(is_mulh), .in5(is_mulhu), .in6(is_slt),
    .in7(is_xor), .in8(is_srl), .in9(is_sra), .in10(is_or), .in11(is_and), .in12(is_lb), .in13(is_lh),
    .in14(is_lw), .in15(is_addi), .in16(is_slli), .in17(is_slti), .in18(is_xori), .in19(is_srli),
    .in20(is_srai), .in21(is_ori), .in22(is_andi), .in23(is_sb), .in24(is_sh), .in25(is_sw), .in26(is_beq),
    .in27(is_bne), .in28(is_blt), .in29(is_bge), .in30(is_bltu), .in31(is_bgeu), .in32(is_auipc),
    .in33(is_lui), .in34(is_jal), .in35(is_jalr), .out(Rom_input));  // open: in36, in37, in38, in39, in40, in41, in42, in43, in44, in45, in46, in47, in48, in49, in50, in51, in52, in53, in54, in55, in56, in57, in58, in59, in60, in61, in62, in63, gs, en_out, en_in

  // Other names for the same wires on the sheet: beq_out = BrEq; blt_out = BrLt; bltu_out = BrLt;
  //   Opcode[6:0] = Instruction[6:0]; Rd[4:0] = Instruction[11:7]; Funct3[2:0] = Instruction[14:12];
  //   Rs1[4:0] = Instruction[19:15]; Rs2[4:0] = Instruction[24:20]; Funct7[6:0] = Instruction[31:25];
  //   isU_Type1 = is_auipc; isJ_Type = is_jal; isU_Type2 = is_lui

  // Notes on the sheet:
  //   INPUTS to your circuit
  //   contents of rom_1 (hex, n*v repeats v):
  //   1001 1401 1601 1081 1481 1581 1101 1201 1281 1681 1301 1381 41 41 41 1041 10c1 1141 1241 12c1 16c1
  //   1341 13c1 842 842 842 4*64 74 74 1067 17e7 2069 2041
  //   ROM FOR CONTROL LOGIC
  //   DON'T CHANGE THE LOCATIONS OF THE INPUTS AND OUTPUTS!
  //   This is only if you choose to do the ROM option
  //   CONNECT
  //   WIRE
  //   TO
  //   USE
  //   ROM
  //   OUTPUT from your circuit
  //   Reminder: If using ROM, use combinational logic for PCSel
  //   If not B type, output 0;
  //   If it is B type, only result selected by funct3 will be rounte to the output. Because funct3 konws instruction is unsigned or signed, there is no need to distinguish blt and bltu
endmodule
