// Logisim project imm-gen.circ as structural Verilog: 1 circuit, main circuit imm_gen
module imm_gen (
  input  [31:0] Instruction,
  input  [2:0] ImmSel,
  output [31:0] Immediate
);

  wire [31:0] B_TypeImme, I_TypeImme, J_TypeImme, S_TypeImme;

  assign I_TypeImme = {{20{Instruction[31]}}, Instruction[31:20]};  // Bit_Extender bit_extender_1
  assign S_TypeImme = {{20{Instruction[31]}}, {Instruction[31:25], Instruction[11:7]}};  // Bit_Extender bit_extender_2
  assign B_TypeImme = {{19{Instruction[31]}}, {Instruction[31], Instruction[7], Instruction[30:25], Instruction[11:8], 1'b0}};  // Bit_Extender bit_extender_3
  assign J_TypeImme = {{11{Instruction[31]}}, {Instruction[31], Instruction[19:12], Instruction[20], Instruction[30:21], 1'b0}};  // Bit_Extender bit_extender_4
  Multiplexer #(.select(3), .width(32)) multiplexer_1 (
    .in0(I_TypeImme), .in1(S_TypeImme), .in2(B_TypeImme), .in3({Instruction[31:12], {12{1'b0}}}),
    .in4(J_TypeImme), .out(Immediate), .sel(ImmSel));  // open: in5, in6, in7

  // Other names for the same wires on the sheet: Bit11to8[3:0] = Instruction[11:8]; Bit7 = Instruction[7];
  //   Bit24to21[3:0] = Instruction[24:21]; U_TypeImme[31:12] = Instruction[31:12];
  //   Bit30to25[5:0] = Instruction[30:25]; Bit20 = Instruction[20]; Bit14to12[2:0] = Instruction[14:12];
  //   Bit19to15[4:0] = Instruction[19:15]; Bit31 = Instruction[31]; Bit6to0[6:0] = Instruction[6:0]

  // Notes on the sheet:
  //   INPUTS to your circuit
  //   DON'T CHANGE THE LOCATIONS OF THE INPUTS AND OUTPUTS!
  //   OUTPUT from your circuit
endmodule
