// Logisim project partial-load.circ as structural Verilog: 1 circuit, main circuit partial_load
module partial_load (
  input  [31:0] Instruction,
  input  [31:0] MemAddress,
  input  [31:0] DataFromMem,
  output [31:0] DataToReg
);

  wire comparator_1_eq;
  wire [31:0] multiplexer_1_out, SignExt0, SignExt1, SignExt2, SignExt3, SignExt4, SignExt5, SignExt6;

  Multiplexer #(.select(4), .width(32)) multiplexer_1 (
    .in0(SignExt0), .in1(SignExt1), .in2(SignExt2), .in3(SignExt3), .in4(SignExt4), .in5(SignExt5),
    .in6(SignExt6), .in8(DataFromMem), .out(multiplexer_1_out), .sel({Instruction[13:12], MemAddress[1:0]}));  // open: in7, in9, in10, in11, in12, in13, in14, in15
  assign SignExt0 = {{24{DataFromMem[7]}}, DataFromMem[7:0]};  // Bit_Extender bit_extender_1
  assign SignExt1 = {{24{DataFromMem[15]}}, DataFromMem[15:8]};  // Bit_Extender bit_extender_2
  assign SignExt2 = {{24{DataFromMem[23]}}, DataFromMem[23:16]};  // Bit_Extender bit_extender_3
  assign SignExt3 = {{24{DataFromMem[31]}}, DataFromMem[31:24]};  // Bit_Extender bit_extender_4
  assign SignExt4 = {{16{DataFromMem[15]}}, DataFromMem[15:0]};  // Bit_Extender bit_extender_5
  assign SignExt5 = {{16{DataFromMem[23]}}, DataFromMem[23:8]};  // Bit_Extender bit_extender_6
  assign SignExt6 = {{16{DataFromMem[31]}}, DataFromMem[31:16]};  // Bit_Extender bit_extender_7
  Comparator #(.mode("unsigned"), .width(7)) comparator_1 (
    .a(7'b0000011), .b(Instruction[6:0]), .eq(comparator_1_eq));  // open: gt, lt
  Multiplexer #(.width(32)) multiplexer_2 (
    .in0({32{1'b0}}), .in1(multiplexer_1_out), .out(DataToReg), .sel(comparator_1_eq));

  // Other names for the same wires on the sheet: Bits7to0[7:0] = DataFromMem[7:0]; SignExt8[31:0] = DataFromMem;
  //   Bits15to8[7:0] = DataFromMem[15:8]; Bits23to16[7:0] = DataFromMem[23:16]; Bits31to24[7:0] = DataFromMem[31:24];
  //   Opcode[6:0] = Instruction[6:0]; Rd[4:0] = Instruction[11:7]; Funct3[2:0] = Instruction[14:12];
  //   Rs1[4:0] = Instruction[19:15]; Rs2[4:0] = Instruction[24:20]; Funct7[6:0] = Instruction[31:25];
  //   MA_Bottom2[1:0] = MemAddress[1:0]; Sel[3:0] = {Instruction[13:12], MemAddress[1:0]};
  //   Funct3_Bottom2[1:0] = Instruction[13:12]

  // Notes on the sheet:
  //   INPUTS to your circuit
  //   DON'T CHANGE THE LOCATIONS OF THE INPUTS AND OUTPUTS!
  //   OUTPUT from your circuit
endmodule
