// Logisim project partial-store.circ as structural Verilog: 1 circuit, main circuit partial_store
module partial_store (
  input  [31:0] Instruction,
  input  [31:0] MemAddress,
  input  [31:0] DataFromReg,
  input  MemWEn,
  output [3:0] MemWriteMask,
  output [31:0] DataToMem
);

  wire [3:0] multiplexer_2_out;
  wire [31:0] multiplexer_1_out;

  Multiplexer #(.select(4), .width(32)) multiplexer_1 (
    .in0({{24{1'b0}}, DataFromReg[7:0]}), .in1({{16{1'b0}}, DataFromReg[7:0], {8{1'b0}}}),
    .in2({{8{1'b0}}, DataFromReg[7:0], {16{1'b0}}}), .in3({DataFromReg[7:0], {24{1'b0}}}),
    .in4({{16{1'b0}}, DataFromReg[15:0]}), .in6({DataFromReg[15:0], {16{1'b0}}}), .in8(DataFromReg),
    .out(multiplexer_1_out), .sel({Instruction[13:12], MemAddress[1:0]}));  // open: in5, in7, in9, in10, in11, in12, in13, in14, in15
  Multiplexer #(.select(4), .width(4)) multiplexer_2 (
    .in0(4'b0001), .in1(4'b0010), .in2(4'b0100), .in3(4'b1000), .in4(4'b0011), .in6(4'b1100), .in8(4'b1111),
    .out(multiplexer_2_out), .sel({Instruction[13:12], MemAddress[1:0]}));  // open: in5, in7, in9, in10, in11, in12, in13, in14, in15
  Multiplexer #(.width(32)) multiplexer_3 (.in0({32{1'b0}}), .in1(multiplexer_1_out), .out(DataToMem), .sel(MemWEn));
  Multiplexer #(.width(4)) multiplexer_4 (.in0(4'b0000), .in1(multiplexer_2_out), .out(MemWriteMask), .sel(MemWEn));

  // Other names for the same wires on the sheet: Bits7to0[7:0] = DataFromReg[7:0]; Ext0[7:0] = DataFromReg[7:0];
  //   Ext1[15:8] = DataFromReg[7:0]; Ext2[23:16] = DataFromReg[7:0]; Ext3[31:24] = DataFromReg[7:0];
  //   Ext4[15:0] = DataFromReg[15:0]; Ext6[31:16] = DataFromReg[15:0]; Ext8[31:0] = DataFromReg;
  //   Bits15to8[7:0] = DataFromReg[15:8]; Bits23to16[7:0] = DataFromReg[23:16]; Bits31to24[7:0] = DataFromReg[31:24];
  //   Opcode[6:0] = Instruction[6:0]; Rd[4:0] = Instruction[11:7]; Funct3[2:0] = Instruction[14:12];
  //   Rs1[4:0] = Instruction[19:15]; Rs2[4:0] = Instruction[24:20]; Funct7[6:0] = Instruction[31:25];
  //   MA_Bottom2[1:0] = MemAddress[1:0]; Sel[3:0] = {Instruction[13:12], MemAddress[1:0]};
  //   Funct3_Bottom2[1:0] = Instruction[13:12]

  // Notes on the sheet:
  //   INPUTS to your circuit
  //   DON'T CHANGE THE LOCATIONS OF THE INPUTS AND OUTPUTS!
  //   OUTPUT from your circuit
endmodule
