// Logisim project regfile.circ as structural Verilog: 1 circuit, main circuit regfile
module regfile (
  input  [4:0] ReadIndex1,
  input  [4:0] ReadIndex2,
  input  [4:0] WriteIndex,
  input  [31:0] WriteData,
  input  RegWEn,
  input  clk,
  output [31:0] ra,
  output [31:0] sp,
  output [31:0] t0,
  output [31:0] t1,
  output [31:0] t2,
  output [31:0] s0,
  output [31:0] s1,
  output [31:0] a0,
  output [31:0] ReadData1,
  output [31:0] ReadData2
);

  wire and_1_out, and_2_out, and_3_out, and_4_out, and_5_out, and_6_out, and_7_out, and_8_out, and_9_out,
       and_10_out, and_11_out, and_12_out, and_13_out, and_14_out, and_15_out, and_16_out, and_17_out,
       and_18_out, and_19_out, and_20_out, and_21_out, and_22_out, and_23_out, and_24_out, and_25_out,
       and_26_out, and_27_out, and_28_out, and_29_out, and_30_out, and_31_out, and_32_out, Reg00WEn,
       Reg01WEn, Reg02WEn, Reg03WEn, Reg04WEn, Reg05WEn, Reg06WEn, Reg07WEn, Reg08WEn, Reg09WEn, Reg10WEn,
       Reg11WEn, Reg12WEn, Reg13WEn, Reg14WEn, Reg15WEn, Reg16WEn, Reg17WEn, Reg18WEn, Reg19WEn, Reg20WEn,
       Reg21WEn, Reg22WEn, Reg23WEn, Reg24WEn, Reg25WEn, Reg26WEn, Reg27WEn, Reg28WEn, Reg29WEn, Reg30WEn,
       Reg31WEn;
  wire [31:0] Reg00Out, Reg03Out, Reg04Out, Reg11Out, Reg12Out, Reg13Out, Reg14Out, Reg15Out, Reg16Out,
       Reg17Out, Reg18Out, Reg19Out, Reg20Out, Reg21Out, Reg22Out, Reg23Out, Reg24Out, Reg25Out, Reg26Out,
       Reg27Out, Reg28Out, Reg29Out, Reg30Out, Reg31Out;

  and and_1 (and_1_out, Reg00WEn, RegWEn);
  and and_2 (and_2_out, Reg01WEn, RegWEn);
  and and_3 (and_3_out, Reg02WEn, RegWEn);
  and and_4 (and_4_out, Reg03WEn, RegWEn);
  and and_5 (and_5_out, Reg04WEn, RegWEn);
  and and_6 (and_6_out, Reg05WEn, RegWEn);
  and and_7 (and_7_out, Reg06WEn, RegWEn);
  and and_8 (and_8_out, Reg07WEn, RegWEn);
  and and_9 (and_9_out, Reg08WEn, RegWEn);
  and and_10 (and_10_out, Reg09WEn, RegWEn);
  and and_11 (and_11_out, Reg10WEn, RegWEn);
  and and_12 (and_12_out, Reg11WEn, RegWEn);
  and and_13 (and_13_out, Reg12WEn, RegWEn);
  and and_14 (and_14_out, Reg13WEn, RegWEn);
  and and_15 (and_15_out, Reg14WEn, RegWEn);
  and and_16 (and_16_out, Reg15WEn, RegWEn);
  Register #(.width(32)) register_1 (.D(WriteData), .en(and_1_out), .clk(clk), .Q(Reg00Out), .clr(1'b1));
  Register #(.width(32)) register_2 (.D(WriteData), .en(and_2_out), .clk(clk), .Q(ra), .clr(1'b0));
  Register #(.width(32)) register_3 (.D(WriteData), .en(and_3_out), .clk(clk), .Q(sp), .clr(1'b0));
  Register #(.width(32)) register_4 (.D(WriteData), .en(and_4_out), .clk(clk), .Q(Reg03Out), .clr(1'b0));
  Register #(.width(32)) register_5 (.D(WriteData), .en(and_5_out), .clk(clk), .Q(Reg04Out), .clr(1'b0));
  Register #(.width(32)) register_6 (.D(WriteData), .en(and_6_out), .clk(clk), .Q(t0), .clr(1'b0));
  Register #(.width(32)) register_7 (.D(WriteData), .en(and_7_out), .clk(clk), .Q(t1), .clr(1'b0));
  Register #(.width(32)) register_8 (.D(WriteData), .en(and_8_out), .clk(clk), .Q(t2), .clr(1'b0));
  Register #(.width(32)) register_9 (.D(WriteData), .en(and_9_out), .clk(clk), .Q(s0), .clr(1'b0));
  Register #(.width(32)) register_10 (.D(WriteData), .en(and_10_out), .clk(clk), .Q(s1), .clr(1'b0));
  Register #(.width(32)) register_11 (.D(WriteData), .en(and_11_out), .clk(clk), .Q(a0), .clr(1'b0));
  Register #(.width(32)) register_12 (.D(WriteData), .en(and_12_out), .clk(clk), .Q(Reg11Out), .clr(1'b0));
  Register #(.width(32)) register_13 (.D(WriteData), .en(and_13_out), .clk(clk), .Q(Reg12Out), .clr(1'b0));
  Register #(.width(32)) register_14 (.D(WriteData), .en(and_14_out), .clk(clk), .Q(Reg13Out), .clr(1'b0));
  Register #(.width(32)) register_15 (.D(WriteData), .en(and_15_out), .clk(clk), .Q(Reg14Out), .clr(1'b0));
  Register #(.width(32)) register_16 (.D(WriteData), .en(and_16_out), .clk(clk), .Q(Reg15Out), .clr(1'b0));
  and and_17 (and_17_out, Reg16WEn, RegWEn);
  and and_18 (and_18_out, Reg17WEn, RegWEn);
  and and_19 (and_19_out, Reg18WEn, RegWEn);
  and and_20 (and_20_out, Reg19WEn, RegWEn);
  and and_21 (and_21_out, Reg20WEn, RegWEn);
  and and_22 (and_22_out, Reg21WEn, RegWEn);
  and and_23 (and_23_out, Reg22WEn, RegWEn);
  and and_24 (and_24_out, Reg23WEn, RegWEn);
  and and_25 (and_25_out, Reg24WEn, RegWEn);
  and and_26 (and_26_out, Reg25WEn, RegWEn);
  and and_27 (and_27_out, Reg26WEn, RegWEn);
  and and_28 (and_28_out, Reg27WEn, RegWEn);
  and and_29 (and_29_out, Reg28WEn, RegWEn);
  and and_30 (and_30_out, Reg29WEn, RegWEn);
  and and_31 (and_31_out, Reg30WEn, RegWEn);
  and and_32 (and_32_out, Reg31WEn, RegWEn);
  Register #(.width(32)) register_17 (.D(WriteData), .en(and_17_out), .clk(clk), .Q(Reg16Out), .clr(1'b0));
  Register #(.width(32)) register_18 (.D(WriteData), .en(and_18_out), .clk(clk), .Q(Reg17Out), .clr(1'b0));
  Register #(.width(32)) register_19 (.D(WriteData), .en(and_19_out), .clk(clk), .Q(Reg18Out), .clr(1'b0));
  Register #(.width(32)) register_20 (.D(WriteData), .en(and_20_out), .clk(clk), .Q(Reg19Out), .clr(1'b0));
  Register #(.width(32)) register_21 (.D(WriteData), .en(and_21_out), .clk(clk), .Q(Reg20Out), .clr(1'b0));
  Register #(.width(32)) register_22 (.D(WriteData), .en(and_22_out), .clk(clk), .Q(Reg21Out), .clr(1'b0));
  Register #(.width(32)) register_23 (.D(WriteData), .en(and_23_out), .clk(clk), .Q(Reg22Out), .clr(1'b0));
  Register #(.width(32)) register_24 (.D(WriteData), .en(and_24_out), .clk(clk), .Q(Reg23Out), .clr(1'b0));
  Register #(.width(32)) register_25 (.D(WriteData), .en(and_25_out), .clk(clk), .Q(Reg24Out), .clr(1'b0));
  Register #(.width(32)) register_26 (.D(WriteData), .en(and_26_out), .clk(clk), .Q(Reg25Out), .clr(1'b0));
  Register #(.width(32)) register_27 (.D(WriteData), .en(and_27_out), .clk(clk), .Q(Reg26Out), .clr(1'b0));
  Register #(.width(32)) register_28 (.D(WriteData), .en(and_28_out), .clk(clk), .Q(Reg27Out), .clr(1'b0));
  Register #(.width(32)) register_29 (.D(WriteData), .en(and_29_out), .clk(clk), .Q(Reg28Out), .clr(1'b0));
  Register #(.width(32)) register_30 (.D(WriteData), .en(and_30_out), .clk(clk), .Q(Reg29Out), .clr(1'b0));
  Register #(.width(32)) register_31 (.D(WriteData), .en(and_31_out), .clk(clk), .Q(Reg30Out), .clr(1'b0));
  Register #(.width(32)) register_32 (.D(WriteData), .en(and_32_out), .clk(clk), .Q(Reg31Out), .clr(1'b0));
  Multiplexer #(.select(5), .width(32)) multiplexer_1 (
    .in0(Reg00Out), .in1(ra), .in2(sp), .in3(Reg03Out), .in4(Reg04Out), .in5(t0), .in6(t1), .in7(t2),
    .in8(s0), .in9(s1), .in10(a0), .in11(Reg11Out), .in12(Reg12Out), .in13(Reg13Out), .in14(Reg14Out),
    .in15(Reg15Out), .in16(Reg16Out), .in17(Reg17Out), .in18(Reg18Out), .in19(Reg19Out), .in20(Reg20Out),
    .in21(Reg21Out), .in22(Reg22Out), .in23(Reg23Out), .in24(Reg24Out), .in25(Reg25Out), .in26(Reg26Out),
    .in27(Reg27Out), .in28(Reg28Out), .in29(Reg29Out), .in30(Reg30Out), .in31(Reg31Out), .out(ReadData1),
    .sel(ReadIndex1));
  Multiplexer #(.select(5), .width(32)) multiplexer_2 (
    .in0(Reg00Out), .in1(ra), .in2(sp), .in3(Reg03Out), .in4(Reg04Out), .in5(t0), .in6(t1), .in7(t2),
    .in8(s0), .in9(s1), .in10(a0), .in11(Reg11Out), .in12(Reg12Out), .in13(Reg13Out), .in14(Reg14Out),
    .in15(Reg15Out), .in16(Reg16Out), .in17(Reg17Out), .in18(Reg18Out), .in19(Reg19Out), .in20(Reg20Out),
    .in21(Reg21Out), .in22(Reg22Out), .in23(Reg23Out), .in24(Reg24Out), .in25(Reg25Out), .in26(Reg26Out),
    .in27(Reg27Out), .in28(Reg28Out), .in29(Reg29Out), .in30(Reg30Out), .in31(Reg31Out), .out(ReadData2),
    .sel(ReadIndex2));
  Decoder #(.enable("false"), .select(5)) decoder_1 (
    .out0(Reg00WEn), .out1(Reg01WEn), .out2(Reg02WEn), .out3(Reg03WEn), .out4(Reg04WEn), .out5(Reg05WEn),
    .out6(Reg06WEn), .out7(Reg07WEn), .out8(Reg08WEn), .out9(Reg09WEn), .out10(Reg10WEn), .out11(Reg11WEn),
    .out12(Reg12WEn), .out13(Reg13WEn), .out14(Reg14WEn), .out15(Reg15WEn), .out16(Reg16WEn),
    .out17(Reg17WEn), .out18(Reg18WEn), .out19(Reg19WEn), .out20(Reg20WEn), .out21(Reg21WEn),
    .out22(Reg22WEn), .out23(Reg23WEn), .out24(Reg24WEn), .out25(Reg25WEn), .out26(Reg26WEn),
    .out27(Reg27WEn), .out28(Reg28WEn), .out29(Reg29WEn), .out30(Reg30WEn), .out31(Reg31WEn), .sel(WriteIndex));

  // Other names for the same wires on the sheet: Reg01Out[31:0] = ra; Reg02Out[31:0] = sp; Reg05Out[31:0] = t0;
  //   Reg06Out[31:0] = t1; Reg07Out[31:0] = t2; Reg08Out[31:0] = s0; Reg09Out[31:0] = s1; Reg10Out[31:0] = a0

  // Notes on the sheet:
  //   INPUTS to your circuit
  //   DON'T CHANGE THE LOCATIONS OF THE INPUTS AND OUTPUTS!
  //   These are DEBUG/TEST outputs from your circuit.
  //   OUTPUTS from your circuit
endmodule
